# Fritzing sketch pdp8-mega (saved by Fritzing 0.9.2b)
breadboards: 1

parts:
  IC2 = 24LC01 [package=THT]
  Part1 = Arduino Mega 2560 (Rev3)
  IC3 = IC, DIP package, 28 pins [chip_label=IC]  # not connected
  IC4 = IC, DIP package, 20 pins [chip_label=IC]  # not connected

nets:
  N1: IC2.SCL_-_I2C_Clock, Part1.D21/SCL
  N2: IC2.WP_-_Write_Protect, Part1.D20/SDA
